// Logisim project control-logic.circ as structural Verilog: 1 circuit, main circuit control_logic
module control_logic (
  input  [31:0] inst,
  input  BrEq,
  input  BrLt,
  output PCSel,
  output RegWEn,
  output [2:0] ImmSel,
  output BrUn,
  output ASel,
  output BSel,
  output [3:0] ALUSel,
  output MemRW,
  output [1:0] WBSel,
  output CSRSel,
  output CSRWen
);

  wire and_2_out, and_3_out, and_6_out, and_7_out, and_8_out, and_9_out, multiplexer_3_out,
       multiplexer_6_out, not_1_out, not_2_out, not_3_out, not_4_out, not_5_out, not_6_out, not_7_out,
       not_8_out, not_9_out, not_10_out, not_11_out, odd_parity_1_out, or_2_out, xor_1_out, xor_2_out,
       xor_3_out;
  wire [3:0] multiplexer_1_out, multiplexer_2_out, multiplexer_4_out, multiplexer_9_out;
  wire [3:2] multiplexer_8_out;
  wire [6:0] multiplexer_7_out;

  and and_1 (CSRWen, inst[6], inst[4], inst[5], not_1_out, not_4_out);
  not not_1 (not_1_out, inst[2]);
  and and_2 (and_2_out, not_2_out, inst[5], not_4_out, inst[6]);
  not not_2 (not_2_out, inst[4]);
  not not_3 (not_3_out, inst[5]);
  or or_1 (BSel, not_2_out, not_3_out, inst[2], inst[6]);
  Multiplexer #(.width(4)) multiplexer_1 (.in0(4'b1111), .in1(4'b0001), .out(multiplexer_1_out), .sel(and_2_out));
  not not_4 (not_4_out, inst[2]);
  and and_3 (and_3_out, not_2_out, inst[5], inst[6]);
  Multiplexer #(.width(4)) multiplexer_2 (.in0(multiplexer_1_out), .in1(4'b0101), .out(multiplexer_2_out), .sel(MemRW));
  and and_4 (MemRW, inst[5], not_2_out, not_5_out);
  not not_5 (not_5_out, inst[6]);
  Multiplexer multiplexer_3 (.in0(xor_1_out), .in1(1'b1), .out(multiplexer_3_out), .sel(inst[2]));
  and and_5 (PCSel, and_3_out, multiplexer_3_out);
  not not_6 (not_6_out, inst[13]);
  Multiplexer #(.width(4)) multiplexer_4 (
    .in0(multiplexer_2_out), .in1(4'b1000), .out(multiplexer_4_out), .sel(and_6_out));
  and and_6 (and_6_out, inst[2], not_5_out);
  xor xor_1 (xor_1_out, inst[12], multiplexer_6_out);
  and and_7 (and_7_out, not_6_out, inst[12]);
  not not_7 (not_7_out, inst[6]);
  Multiplexer #(.width(4)) multiplexer_5 (
    .in0(multiplexer_4_out), .in1(4'b1011), .out({RegWEn, ImmSel}), .sel(inst[3]));
  Multiplexer multiplexer_6 (.in0(BrEq), .in1(BrLt), .out(multiplexer_6_out), .sel(inst[14]));
  not not_8 (not_8_out, inst[2]);
  not not_9 (not_9_out, inst[3]);
  Multiplexer #(.width(7)) multiplexer_7 (.in0({7{1'b0}}), .in1(inst[31:25]), .out(multiplexer_7_out), .sel(or_2_out));
  or or_2 (or_2_out, and_7_out, inst[5]);
  and and_8 (and_8_out, not_8_out, not_9_out, inst[4]);
  and and_9 (and_9_out, inst[5], inst[4], inst[2], not_7_out);
  Multiplexer multiplexer_8 (.in0(inst[14]), .in1(1'b1), .out(multiplexer_8_out[2]), .sel(multiplexer_7_out[5]));
  or or_3 (multiplexer_8_out[3], multiplexer_7_out[5], multiplexer_7_out[0]);
  xor xor_2 (xor_2_out, inst[6], inst[5]);
  Multiplexer #(.width(4)) multiplexer_9 (
    .in0(4'b0000), .in1({multiplexer_8_out, inst[13:12]}), .out(multiplexer_9_out), .sel(and_8_out));
  Multiplexer #(.width(4)) multiplexer_10 (.in0(multiplexer_9_out), .in1(4'b1111), .out(ALUSel), .sel(and_9_out));
  xor xor_3 (xor_3_out, inst[4], inst[6]);
  not not_10 (not_10_out, xor_2_out);
  xor odd_parity_1 (odd_parity_1_out, inst[2], inst[3], inst[4], inst[5], inst[6]);
  not not_11 (not_11_out, odd_parity_1_out);
  and and_10 (ASel, not_11_out, xor_3_out, not_10_out);

  assign BrUn = inst[13];
  assign CSRSel = inst[14];
  assign WBSel = {inst[6], inst[4]};

  // Other names for the same wires on the sheet: funct3[2:0] = inst[14:12]; opcode[6:0] = inst[6:0];
  //   funct7[6:0] = inst[31:25]

  // Notes on the sheet:
  //   INPUTS to your circuit
  //   I
  //   SB
  //   If BSel = 1, use imm instead of rs2.
  //   S
  //   U
  //   DON'T CHANGE THE LOCATIONS OF THE INPUTS AND OUTPUTS!
  //   OUTPUT from your circuit
  //   UJ
  //   When ASel=1, use PC instead of rs1 as one operand of ALU.
endmodule
