// Logisim project cpu.circ as structural Verilog: 1 circuit, main circuit cpu
module cpu (
  input  clk,
  input  [31:0] INSTRUCTION,
  input  [31:0] READ_DATA,
  output [31:0] WRITE_ADDRESS,
  output [31:0] PROGRAM_COUNTER,
  output [31:0] ra,
  output [31:0] sp,
  output [31:0] t0,
  output [31:0] t1,
  output [31:0] t2,
  output [31:0] s0,
  output [31:0] s1,
  output [31:0] a0,
  output [31:0] tohost,
  output [3:0] WRITE_ENABLE,
  output [31:0] WRITE_DATA
);

  wire ASel, BrEq, BrLt, BrUn, BSel, control_logic_1_csrsel, control_logic_1_csrwen, MemRW, not_1_out, PCSel,
       RegWEn;
  wire [1:0] WBSel;
  wire [1:1] or_1_out;
  wire [2:0] control_logic_1_immsel;
  wire [3:0] ALUSel, multiplexer_7_out;
  wire [4:3] bit_extender_2_out;
  wire [7:0] multiplexer_8_out;
  wire [15:0] multiplexer_9_out;
  wire [31:0] bit_extender_1_out, bit_extender_3_out, bit_extender_4_out, imm_gen_1_imm, multiplexer_1_out,
       multiplexer_2_out, multiplexer_3_out, multiplexer_4_out, multiplexer_5_out, multiplexer_10_out, PC_4,
       regfile_1_read_data_1, regfile_1_read_data_2, Write_Data_t;

  Adder #(.width(32)) adder_1 (.a(PROGRAM_COUNTER), .b(32'h4), .out(PC_4));  // open: cin, cout
  Register #(.width(32)) PC (.D(multiplexer_1_out), .clk(clk), .Q(PROGRAM_COUNTER));  // open: en, clr
  Multiplexer #(.width(32)) multiplexer_1 (.in0(PC_4), .in1(WRITE_ADDRESS), .out(multiplexer_1_out), .sel(PCSel));
  control_logic control_logic_1 (
    .CSRWen(control_logic_1_csrwen), .PCSel(PCSel), .RegWEn(RegWEn), .ImmSel(control_logic_1_immsel),
    .BrUn(BrUn), .ASel(ASel), .BSel(BSel), .ALUSel(ALUSel), .MemRW(MemRW), .WBSel(WBSel),
    .CSRSel(control_logic_1_csrsel), .inst(INSTRUCTION), .BrEq(BrEq), .BrLt(BrLt));
  imm_gen imm_gen_1 (.inst(INSTRUCTION), .ImmSel(control_logic_1_immsel), .imm(imm_gen_1_imm));
  assign bit_extender_1_out = {{27{1'b0}}, INSTRUCTION[19:15]};  // Bit_Extender bit_extender_1
  Multiplexer #(.width(32)) multiplexer_2 (
    .in0(regfile_1_read_data_1), .in1(bit_extender_1_out), .out(multiplexer_2_out),
    .sel(control_logic_1_csrsel));
  regfile regfile_1 (
    .rs1(INSTRUCTION[19:15]), .rs2(INSTRUCTION[24:20]), .rd(INSTRUCTION[11:7]), .Write_Data(Write_Data_t),
    .RegWEn(RegWEn), .clk(clk), .ra(ra), .sp(sp), .t0(t0), .t1(t1), .t2(t2), .s0(s0), .s1(s1), .a0(a0),
    .Read_Data_1(regfile_1_read_data_1), .Read_Data_2(regfile_1_read_data_2));
  Multiplexer #(.width(32)) multiplexer_3 (
    .in0(regfile_1_read_data_2), .in1(imm_gen_1_imm), .out(multiplexer_3_out), .sel(BSel));
  Shifter #(.width(32)) shifter_1 (.in(regfile_1_read_data_2), .\dist ({bit_extender_2_out, 3'b000}), .out(WRITE_DATA));
  Multiplexer #(.width(32)) multiplexer_4 (
    .in0(regfile_1_read_data_1), .in1(PROGRAM_COUNTER), .out(multiplexer_4_out), .sel(ASel));
  alu alu_1 (.Result(WRITE_ADDRESS), .A(multiplexer_4_out), .B(multiplexer_3_out), .ALUSel(ALUSel));
  branch_comp branch_comp_1 (
    .rs1(regfile_1_read_data_1), .rs2(regfile_1_read_data_2), .BrUn(BrUn), .BrEq(BrEq), .BrLt(BrLt));
  // csr csr_1: pin names not known; wires that end beside it: INSTRUCTION[31:20], multiplexer_2_out, control_logic_1_csrwen, clk, tohost
  Bit_Extender #(.in_width(32), .out_width(2), .\type ("zero")) bit_extender_2 (
    .in(WRITE_ADDRESS), .out(bit_extender_2_out));
  not not_1 (not_1_out, INSTRUCTION[13]);
  Multiplexer #(.width(32)) multiplexer_5 (
    .in0(READ_DATA), .in1(multiplexer_10_out), .out(multiplexer_5_out), .sel(not_1_out));
  Multiplexer #(.select(2), .width(32)) multiplexer_6 (
    .in0(multiplexer_5_out), .in1(WRITE_ADDRESS), .in2(PC_4), .out(Write_Data_t), .sel(WBSel));  // open: in3
  or or_1 (or_1_out[1], INSTRUCTION[13], INSTRUCTION[12]);
  Multiplexer #(.width(4)) multiplexer_7 (
    .in0(4'b0000), .in1({{2{INSTRUCTION[13]}}, or_1_out[1], 1'b1}), .out(multiplexer_7_out), .sel(MemRW));
  Multiplexer #(.select(2), .width(8)) multiplexer_8 (
    .in0(READ_DATA[7:0]), .in1(READ_DATA[15:8]), .in2(READ_DATA[23:16]), .in3(READ_DATA[31:24]),
    .out(multiplexer_8_out), .sel(bit_extender_2_out));
  Multiplexer #(.select(2), .width(16)) multiplexer_9 (
    .in0(READ_DATA[15:0]), .in1(READ_DATA[23:8]), .in2(READ_DATA[31:16]), .out(multiplexer_9_out),
    .sel(bit_extender_2_out));  // open: in3
  Shifter #(.width(4)) shifter_2 (.in(multiplexer_7_out), .\dist (bit_extender_2_out), .out(WRITE_ENABLE));
  assign bit_extender_3_out = {{24{multiplexer_8_out[7]}}, multiplexer_8_out};  // Bit_Extender bit_extender_3
  assign bit_extender_4_out = {{16{multiplexer_9_out[15]}}, multiplexer_9_out};  // Bit_Extender bit_extender_4
  Multiplexer #(.width(32)) multiplexer_10 (
    .in0(bit_extender_3_out), .in1(bit_extender_4_out), .out(multiplexer_10_out), .sel(INSTRUCTION[12]));

  // Other names for the same wires on the sheet: funct3[2:0] = INSTRUCTION[14:12]; ALU_Result[31:0] = WRITE_ADDRESS;
  //   CSR_Address[11:0] = INSTRUCTION[31:20]; rs1[4:0] = INSTRUCTION[19:15]

  // Notes on the sheet:
  //   Output to IMEM
  //   IMEM (do **NOT** move this)
  //   Inputs from IMEM
  //   It is OK to move the PC, RegFile, ALU, MEM, Branch Comp, Imm Gen, and Control Logic to wherever is most convenient for you when constructing your CPU, and to delete this text
  //   Inputs/Outputs for testing. Do **NOT** move these.
  //   Outputs To DMEM
  //   DMEM (do **NOT** move this)
  //   Inputs From DMEM
endmodule
