// Logisim project imm-gen.circ as structural Verilog: 1 circuit, main circuit imm_gen
module imm_gen (
  input  [31:0] inst,
  input  [2:0] ImmSel,
  output [31:0] imm
);

  wire not_1_out, or_1_out;
  wire [0:0] multiplexer_1_out;
  wire [3:0] multiplexer_2_out;
  wire [7:0] multiplexer_4_out;
  wire [11:11] multiplexer_3_out;
  wire [31:0] shifter_1_out;

  Shifter #(.shift("ar"), .width(32)) shifter_1 (.in(inst), .\dist (5'b10100), .out(shifter_1_out));
  Multiplexer #(.select(2)) multiplexer_1 (
    .in0(1'b0), .in1(1'b0), .in2(inst[7]), .in3(shifter_1_out[0]), .out(multiplexer_1_out[0]),
    .sel(ImmSel[2:1]));
  Multiplexer #(.width(4)) multiplexer_2 (
    .in0(inst[11:8]), .in1(shifter_1_out[4:1]), .out(multiplexer_2_out), .sel(ImmSel[1]));
  Multiplexer #(.select(2)) multiplexer_3 (
    .in0(inst[7]), .in1(shifter_1_out[0]), .in2(shifter_1_out[11]), .in3(shifter_1_out[11]),
    .out(multiplexer_3_out[11]), .sel(ImmSel[2:1]));
  Multiplexer #(.width(8)) multiplexer_4 (
    .in0(inst[19:12]), .in1(shifter_1_out[19:12]), .out(multiplexer_4_out), .sel(or_1_out));
  or or_1 (or_1_out, ImmSel[2], not_1_out);
  not not_1 (not_1_out, ImmSel[1]);
  Multiplexer #(.width(32)) multiplexer_5 (
    .in0({inst[31:12], {12{1'b0}}}),
    .in1({shifter_1_out[31:20], multiplexer_4_out, multiplexer_3_out[11], shifter_1_out[10:5], multiplexer_2_out, multiplexer_1_out[0]}),
    .out(imm), .sel(ImmSel[0]));

  // Notes on the sheet:
  //   INPUTS to your circuit
  //   imm[0]
  //   I 111
  //   S 101
  //   SB 001
  //   U 000
  //   UJ 011
  //   DON'T CHANGE THE LOCATIONS OF THE INPUTS AND OUTPUTS!
  //   imm[11]
  //   imm[12:19]
  //   OUTPUT from your circuit
endmodule
