// Logisim project regfile.circ as structural Verilog: 1 circuit, main circuit regfile
module regfile (
  input  [4:0] rs1,
  input  [4:0] rs2,
  input  [4:0] rd,
  input  [31:0] Write_Data,
  input  RegWEn,
  input  clk,
  output [31:0] ra,
  output [31:0] sp,
  output [31:0] t0,
  output [31:0] t1,
  output [31:0] t2,
  output [31:0] s0,
  output [31:0] s1,
  output [31:0] a0,
  output [31:0] Read_Data_1,
  output [31:0] Read_Data_2
);

  wire we1, we2, we3, we4, we5, we6, we7, we8, we9, we10, we11, we12, we13, we14, we15, we16, we17, we18,
       we19, we20, we21, we22, we23, we24, we25, we26, we27, we28, we29, we30, we31;
  wire [31:0] q3, q4, q11, q12, q13, q14, q15, q16, q17, q18, q19, q20, q21, q22, q23, q24, q25, q26, q27,
       q28, q29, q30, q31;

  Register #(.width(32)) x4 (.D(Write_Data), .en(we4), .clk(clk), .Q(q4), .clr(1'b0));
  Register #(.width(32)) x8 (.D(Write_Data), .en(we8), .clk(clk), .Q(s0), .clr(1'b0));
  Register #(.width(32)) x12 (.D(Write_Data), .en(we12), .clk(clk), .Q(q12), .clr(1'b0));
  Register #(.width(32)) x16 (.D(Write_Data), .en(we16), .clk(clk), .Q(q16), .clr(1'b0));
  Register #(.width(32)) x20 (.D(Write_Data), .en(we20), .clk(clk), .Q(q20), .clr(1'b0));
  Register #(.width(32)) x24 (.D(Write_Data), .en(we24), .clk(clk), .Q(q24), .clr(1'b0));
  Register #(.width(32)) x28 (.D(Write_Data), .en(we28), .clk(clk), .Q(q28), .clr(1'b0));
  Register #(.width(32)) x1 (.D(Write_Data), .en(we1), .clk(clk), .Q(ra), .clr(1'b0));
  Register #(.width(32)) x5 (.D(Write_Data), .en(we5), .clk(clk), .Q(t0), .clr(1'b0));
  Register #(.width(32)) x9 (.D(Write_Data), .en(we9), .clk(clk), .Q(s1), .clr(1'b0));
  Register #(.width(32)) x13 (.D(Write_Data), .en(we13), .clk(clk), .Q(q13), .clr(1'b0));
  Register #(.width(32)) x17 (.D(Write_Data), .en(we17), .clk(clk), .Q(q17), .clr(1'b0));
  Register #(.width(32)) x21 (.D(Write_Data), .en(we21), .clk(clk), .Q(q21), .clr(1'b0));
  Register #(.width(32)) x25 (.D(Write_Data), .en(we25), .clk(clk), .Q(q25), .clr(1'b0));
  Register #(.width(32)) x29 (.D(Write_Data), .en(we29), .clk(clk), .Q(q29), .clr(1'b0));
  Demultiplexer #(.select(5)) demultiplexer_1 (
    .out1(we1), .out2(we2), .out3(we3), .out4(we4), .out5(we5), .out6(we6), .out7(we7), .out8(we8),
    .out9(we9), .out10(we10), .out11(we11), .out12(we12), .out13(we13), .out14(we14), .out15(we15),
    .out16(we16), .out17(we17), .out18(we18), .out19(we19), .out20(we20), .out21(we21), .out22(we22),
    .out23(we23), .out24(we24), .out25(we25), .out26(we26), .out27(we27), .out28(we28), .out29(we29),
    .out30(we30), .out31(we31), .in(RegWEn), .sel(rd));  // open: out0
  Register #(.width(32)) x2 (.D(Write_Data), .en(we2), .clk(clk), .Q(sp), .clr(1'b0));
  Register #(.width(32)) x6 (.D(Write_Data), .en(we6), .clk(clk), .Q(t1), .clr(1'b0));
  Register #(.width(32)) x10 (.D(Write_Data), .en(we10), .clk(clk), .Q(a0), .clr(1'b0));
  Register #(.width(32)) x14 (.D(Write_Data), .en(we14), .clk(clk), .Q(q14), .clr(1'b0));
  Register #(.width(32)) x18 (.D(Write_Data), .en(we18), .clk(clk), .Q(q18), .clr(1'b0));
  Register #(.width(32)) x22 (.D(Write_Data), .en(we22), .clk(clk), .Q(q22), .clr(1'b0));
  Register #(.width(32)) x26 (.D(Write_Data), .en(we26), .clk(clk), .Q(q26), .clr(1'b0));
  Register #(.width(32)) x30 (.D(Write_Data), .en(we30), .clk(clk), .Q(q30), .clr(1'b0));
  Register #(.width(32)) x3 (.D(Write_Data), .en(we3), .clk(clk), .Q(q3), .clr(1'b0));
  Register #(.width(32)) x7 (.D(Write_Data), .en(we7), .clk(clk), .Q(t2), .clr(1'b0));
  Register #(.width(32)) x11 (.D(Write_Data), .en(we11), .clk(clk), .Q(q11), .clr(1'b0));
  Register #(.width(32)) x15 (.D(Write_Data), .en(we15), .clk(clk), .Q(q15), .clr(1'b0));
  Register #(.width(32)) x19 (.D(Write_Data), .en(we19), .clk(clk), .Q(q19), .clr(1'b0));
  Register #(.width(32)) x23 (.D(Write_Data), .en(we23), .clk(clk), .Q(q23), .clr(1'b0));
  Register #(.width(32)) x27 (.D(Write_Data), .en(we27), .clk(clk), .Q(q27), .clr(1'b0));
  Register #(.width(32)) x31 (.D(Write_Data), .en(we31), .clk(clk), .Q(q31), .clr(1'b0));
  Multiplexer #(.select(5), .width(32)) multiplexer_1 (
    .in0({32{1'b0}}), .in1(ra), .in2(sp), .in3(q3), .in4(q4), .in5(t0), .in6(t1), .in7(t2), .in8(s0),
    .in9(s1), .in10(a0), .in11(q11), .in12(q12), .in13(q13), .in14(q14), .in15(q15), .in16(q16), .in17(q17),
    .in18(q18), .in19(q19), .in20(q20), .in21(q21), .in22(q22), .in23(q23), .in24(q24), .in25(q25),
    .in26(q26), .in27(q27), .in28(q28), .in29(q29), .in30(q30), .in31(q31), .out(Read_Data_1), .sel(rs1));
  Multiplexer #(.select(5), .width(32)) multiplexer_2 (
    .in0({32{1'b0}}), .in1(ra), .in2(sp), .in3(q3), .in4(q4), .in5(t0), .in6(t1), .in7(t2), .in8(s0),
    .in9(s1), .in10(a0), .in11(q11), .in12(q12), .in13(q13), .in14(q14), .in15(q15), .in16(q16), .in17(q17),
    .in18(q18), .in19(q19), .in20(q20), .in21(q21), .in22(q22), .in23(q23), .in24(q24), .in25(q25),
    .in26(q26), .in27(q27), .in28(q28), .in29(q29), .in30(q30), .in31(q31), .out(Read_Data_2), .sel(rs2));

  // Other names for the same wires on the sheet: q1[31:0] = ra; q2[31:0] = sp; q5[31:0] = t0; q6[31:0] = t1;
  //   q7[31:0] = t2; q8[31:0] = s0; q9[31:0] = s1; q10[31:0] = a0; read_data1[31:0] = Read_Data_1;
  //   read_data2[31:0] = Read_Data_2; read_reg1[4:0] = rs1; read_reg2[4:0] = rs2; write_en = RegWEn;
  //   write_reg[4:0] = rd

  // Notes on the sheet:
  //   INPUTS to your circuit
  //   DON'T CHANGE THE LOCATIONS OF THE INPUTS AND OUTPUTS!
  //   These are DEBUG/TEST outputs from your circuit.
  //   OUTPUTS from your circuit
endmodule
