// Logisim project cpu-ex1.circ as structural Verilog: 1 circuit, main circuit run_main
module run_main (
  output [31:0] ra,
  output [31:0] sp,
  output [31:0] t0,
  output [31:0] t1,
  output [31:0] t2,
  output [31:0] s0,
  output [31:0] s1,
  output [31:0] a0,
  output [31:0] Requested_Address,
  output [31:0] Requested_Instruction,
  output [15:0] Time_Step,
  output halt
);

  wire clk;

  Clock clock_1 (.out(clk));
  // Probe on Requested_Address
  // cpu_harness cpu_harness_1: pin names not known; wires that end beside it: Requested_Instruction, clk, Requested_Address, ra, sp, t0, t1, t2, s0, s1, a0
  ROM #(.addrWidth(14), .dataWidth(32)) rom_1 (.addr(Requested_Address[15:2]), .data(Requested_Instruction));
  // Probe on Requested_Instruction
  Counter #(.max('hffff), .width(16)) counter_1 (.clk(clk), .Q(Time_Step));  // open: clr, load, up, count, D, carry
  Comparator #(.width(16)) comparator_1 (.a(Time_Step), .b(16'h38), .eq(halt));  // open: gt, lt

  // Other names for the same wires on the sheet: INSTRUCTION[31:0] = Requested_Instruction;
  //   PROGRAM_COUNTER[31:0] = Requested_Address

  // Notes on the sheet:
  //   contents of rom_1 (hex, n*v repeats v):
  //   600293 8000313 532423 2B3 100313 8800E13 E2E03 E0C63 5303B3 30293 38313 FFFE0E13 FEDFF06F 100513
  //   28593 A00513
  //   Instruction Memory
  //   Halts Execution After Constant # of Clock Cycles
  //   Constant
endmodule
